# Fritzing sketch Sketch (saved by Fritzing 1.0.1rc)

parts:
  ZS-042_RTC1 = ZS-042 RTC Module
  microSD1 = MicroSD Card Module
  DHT11_1 = DHT11 module
  Capacitive_Soil_Moisture_Sensor1 = DFRobot Capacitive Soil Moisture Sensor V1.0 [part_number=SEN0193]
  Capacitive_Soil_Moisture_Sensor2 = DFRobot Capacitive Soil Moisture Sensor V1.0 [part_number=SEN0193]
  Capacitive_Soil_Moisture_Sensor4 = DFRobot Capacitive Soil Moisture Sensor V1.0 [part_number=SEN0193]
  Capacitive_Soil_Moisture_Sensor5 = DFRobot Capacitive Soil Moisture Sensor V1.0 [part_number=SEN0193]
  Capacitive_Soil_Moisture_Sensor6 = DFRobot Capacitive Soil Moisture Sensor V1.0 [part_number=SEN0193]
  Part3 = LCD1602-I2C
  Part4 = Arduino Nano (Rev3.0) (ICSP)

nets:
  GND: ZS-042_RTC1.GND, microSD1.GND, DHT11_1.GND, Capacitive_Soil_Moisture_Sensor1.GND, Capacitive_Soil_Moisture_Sensor2.GND, Capacitive_Soil_Moisture_Sensor4.GND, Capacitive_Soil_Moisture_Sensor5.GND, Capacitive_Soil_Moisture_Sensor6.GND, Part3.GND, Part4.GND
  VCC: ZS-042_RTC1.VCC, DHT11_1.VCC, Part4.3V3
  N1: ZS-042_RTC1.SDA, Part3.SDA, Part4.A4
  N2: ZS-042_RTC1.SCL, Part3.SCL, Part4.A5
  VCC_2: microSD1.VCC, Capacitive_Soil_Moisture_Sensor1.VCC, Capacitive_Soil_Moisture_Sensor2.VCC, Capacitive_Soil_Moisture_Sensor4.VCC, Capacitive_Soil_Moisture_Sensor5.VCC, Capacitive_Soil_Moisture_Sensor6.VCC, Part3.VCC, Part4.5V
  N3: microSD1.MISO, Part4.D12/MISO
  N4: microSD1.MOSI, Part4.D11/MOSI
  N5: microSD1.SCK, Part4.D13/SCK
  N6: microSD1.CS, Part4.D4
  N7: DHT11_1.DATA, Part4.D2
  N8: Capacitive_Soil_Moisture_Sensor1.A, Part4.A0
  N9: Capacitive_Soil_Moisture_Sensor2.A, Part4.A1
  N10: Capacitive_Soil_Moisture_Sensor4.A, Part4.A3
  N11: Capacitive_Soil_Moisture_Sensor5.A, Part4.A2
  N12: Capacitive_Soil_Moisture_Sensor6.A, Part4.A6

custom parts:
  MicroSD Card Module: A common microSD card module.
  DHT11 module: https://cdn-learn.adafruit.com/downloads/pdf/dht.pdf DHT11 black pcb module reference by:https://github.com/adafruit/Fritzing-Library/blob/master/parts/DHT11%20Humitidy%20and%20Temperature%20Sensor.fzpz
  DFRobot Capacitive Soil Moisture Sensor V1.0: DFRobot Capacitive Soil Moisture Sensor V1.0 This product measures soil moisture levels by capacitive sensing, rather than resistive sensing like other types of moisture sensor. It is made of a corrosion resistant material giving it a long service life. Insert it into soil and impress your friends with the real-time soil moisture data! The product includes an on-board voltage regulator which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
  LCD1602-I2C: A standard character display, usually with 2x16 characters. Comes in many colors with LCM1602 IIC attached.
